# Fritzing sketch scheme-fritzing (saved by Fritzing 1.0.1rc)
stripboards: 1

parts:
  Composant1 = Arduino Uno (Rev3)
  R1 = Resistor [tolerance=±5% resistance=220 package="0402 [SMD]"]
  R2 = Resistor [tolerance=±5% resistance=220 package="0402 [SMD]"]
  R3 = Resistor [tolerance=±5% resistance=220 package="0402 [SMD]"]
  R4 = Resistor [tolerance=±5% resistance=220 package="0402 [SMD]"]
  LED4 = smd LED [color="Red (633nm)" package="0805 [SMD]"]
  LED5 = smd LED [color="Red (633nm)" package="0805 [SMD]"]
  LED6 = smd LED [color="Red (633nm)" package="0805 [SMD]"]
  LED7 = smd LED [color="Red (633nm)" package="0805 [SMD]"]
  S5 = Round Pushbutton
  S1 = Round Pushbutton
  S2 = Round Pushbutton
  S4 = Round Pushbutton
  S3 = Round Pushbutton

nets:
  N1: Composant1.D9_PWM, S1.leg1
  N2: Composant1.D10_PWM/SS, S2.leg1
  N3: Composant1.D11_PWM/MOSI, S3.leg1
  N4: Composant1.D12/MISO, S4.leg1
  N5: Composant1.D13/SCK, S5.leg1
  N6: Composant1.GND, LED4.cathode, LED5.cathode, LED6.cathode, LED7.cathode, S5.leg0, S1.leg0, S2.leg0, S4.leg0, S3.leg0
  N7: Composant1.D2, R4.Pin_1
  N8: Composant1.D3_PWM, R2.Pin_1
  N9: Composant1.D4, R3.Pin_1
  N10: Composant1.D5_PWM, R1.Pin_1
  N11: R1.Pin_0, LED7.anode
  N12: R2.Pin_0, LED5.anode
  N13: R3.Pin_0, LED6.anode
  N14: R4.Pin_0, LED4.anode
